// Digital circuit tellertje.dig as structural Verilog
module tellertje (
  input  clk
);

  wire _7411_1_pin6, _7411_1_pin8, _7411_1_pin11, _7411_1_pin12, _7421_1_pin6, _7421_1_pin8, _7421_1_pin9,
       _7421_2_pin6, _7421_2_pin8, _7486_1_pin3, _7486_1_pin6, _7486_1_pin8, _7486_1_pin11, _74163_1_pin1,
       _74163_1_pin15, _74163_2_pin1, _74163_2_pin10, _74163_2_pin15, _74163_3_pin15, _74163_4_pin15,
       _74163_7_pin15, _74163_8_pin15, _74163_9_pin15, _74163_10_pin15, a0, a1, a2, a3, a4, a5, a6, a7, a8,
       a9, a10, a11, a12, a13, a14, a15, a16, a17, a18, d_ff_1_q, not_3_out, q0, q1, q2, q3, q4, q5, q6, q7,
       q8, q9, rs_ff_as_2_q, rs_ff_as_3_q, rs_ff_as_4_q, rs_ff_as_6_q, y0, y1, y2, y3, y4, y5, y6, y7, y8, y9;

  _74163 _74163_1 (
    .pin1(_74163_1_pin1), .pin2(clk), .pin3(1'b0), .pin4(1'b0), .pin5(1'b0), .pin6(1'b0), .pin7(1'b1),
    .pin8(1'b0), .pin9(1'b1), .pin10(1'b1), .pin11(q3), .pin12(q2), .pin13(q1), .pin14(q0),
    .pin15(_74163_1_pin15), .pin16(1'b1));
  _74163 _74163_2 (
    .pin1(_74163_2_pin1), .pin2(clk), .pin3(1'b0), .pin4(1'b0), .pin5(1'b0), .pin6(1'b0), .pin7(1'b1),
    .pin8(1'b0), .pin9(1'b1), .pin10(_74163_2_pin10), .pin11(y3), .pin12(y2), .pin13(y1), .pin14(y0),
    .pin15(_74163_2_pin15), .pin16(1'b1));
  // Probe on {q9, q8, q7, q6, q5, q4, q3, q2, q1, q0}
  // Probe on {y9, y8, y7, y6, y5, y4, y3, y2, y1, y0}
  _74163 _74163_3 (
    .pin1(_74163_1_pin1), .pin2(clk), .pin3(1'b0), .pin4(1'b0), .pin5(1'b0), .pin6(1'b0), .pin7(1'b1),
    .pin8(1'b0), .pin9(1'b1), .pin10(_74163_1_pin15), .pin11(q7), .pin12(q6), .pin13(q5), .pin14(q4),
    .pin15(_74163_3_pin15), .pin16(1'b1));
  _74163 _74163_4 (
    .pin1(_74163_2_pin1), .pin2(clk), .pin3(1'b0), .pin4(1'b0), .pin5(1'b0), .pin6(1'b0), .pin7(1'b1),
    .pin8(1'b0), .pin9(1'b1), .pin10(_74163_2_pin15), .pin11(y7), .pin12(y6), .pin13(y5), .pin14(y4),
    .pin15(_74163_4_pin15), .pin16(1'b1));
  _7421 _7421_1 (
    .pin1(y5), .pin2(y6), .pin4(y7), .pin5(y8), .pin6(_7421_1_pin6), .pin7(1'b0), .pin8(_7421_1_pin8),
    .pin9(_7421_1_pin9), .pin10(y1), .pin12(y3), .pin13(1'b1), .pin14(1'b1));  // open: pin3, pin11
  _7421 _7421_2 (
    .pin1(y9), .pin2(y0), .pin4(y2), .pin5(y3), .pin6(_7421_2_pin6), .pin7(1'b0), .pin8(_7421_2_pin8),
    .pin9(_7421_1_pin9), .pin10(1'b1), .pin12(y2), .pin13(y3), .pin14(1'b1));  // open: pin3, pin11
  _74163 _74163_5 (
    .pin1(_74163_1_pin1), .pin2(clk), .pin3(1'b0), .pin4(1'b0), .pin5(1'b0), .pin6(1'b0), .pin7(1'b1),
    .pin8(1'b0), .pin9(1'b1), .pin10(_74163_3_pin15), .pin13(q9), .pin14(q8), .pin16(1'b1));  // open: pin11, pin12, pin15
  _7411 _7411_1 (
    .pin1(q7), .pin2(q9), .pin3(q7), .pin4(q9), .pin5(q4), .pin6(_7411_1_pin6), .pin7(1'b0),
    .pin8(_7411_1_pin8), .pin9(q6), .pin10(q5), .pin11(_7411_1_pin11), .pin12(_7411_1_pin12), .pin13(1'b1),
    .pin14(1'b1));
  _7411 _7411_2 (
    .pin1(1'b0), .pin2(1'b0), .pin3(q5), .pin4(q9), .pin5(q8), .pin6(_74163_2_pin10), .pin7(1'b0),
    .pin9(1'b0), .pin10(1'b0), .pin11(1'b0), .pin13(1'b0), .pin14(1'b1));  // open: pin8, pin12
  not not_1 (_74163_1_pin1, _74163_2_pin10);
  not not_2 (_74163_2_pin1, _7421_2_pin6);
  _74163 _74163_6 (
    .pin1(_74163_2_pin1), .pin2(clk), .pin3(1'b0), .pin4(1'b0), .pin5(1'b0), .pin6(1'b0), .pin7(1'b1),
    .pin8(1'b0), .pin9(1'b1), .pin10(_74163_4_pin15), .pin13(y9), .pin14(y8), .pin16(1'b1));  // open: pin11, pin12, pin15
  RS_FF_AS rs_ff_as_1 (.S(_7421_1_pin6), .R(_7421_2_pin6), .Q(_7421_1_pin9));  // open: nQ
  RS_FF_AS rs_ff_as_2 (.S(_7421_1_pin8), .R(_7421_2_pin6), .Q(rs_ff_as_2_q));  // open: nQ
  RS_FF_AS rs_ff_as_3 (.S(_7421_2_pin8), .R(_7421_2_pin6), .Q(rs_ff_as_3_q));  // open: nQ
  Break #(.Cycles(1000000)) break_1 (.brk(_7421_1_pin9));
  RS_FF_AS rs_ff_as_4 (.S(_7411_1_pin12), .R(_74163_2_pin10), .Q(rs_ff_as_4_q));  // open: nQ
  RS_FF_AS rs_ff_as_5 (.S(_7411_1_pin6), .R(_74163_2_pin10), .Q(_7411_1_pin11));  // open: nQ
  RS_FF_AS rs_ff_as_6 (.S(_7411_1_pin8), .R(_74163_2_pin10), .Q(rs_ff_as_6_q));  // open: nQ
  _7486 _7486_1 (
    .pin1(_7411_1_pin11), .pin2(rs_ff_as_6_q), .pin3(_7486_1_pin3), .pin4(rs_ff_as_3_q), .pin5(rs_ff_as_2_q),
    .pin6(_7486_1_pin6), .pin7(1'b0), .pin8(_7486_1_pin8), .pin9(_7421_1_pin9), .pin10(1'b1),
    .pin11(_7486_1_pin11), .pin12(rs_ff_as_4_q), .pin13(1'b1), .pin14(1'b1));
  LED led_1 (.in(_7421_1_pin9));
  LED led_2 (.in(rs_ff_as_2_q));
  LED led_3 (.in(rs_ff_as_3_q));
  LED led_4 (.in(rs_ff_as_4_q));
  LED led_5 (.in(_7411_1_pin11));
  LED led_6 (.in(rs_ff_as_6_q));
  LED led_7 (.in(_7486_1_pin3));
  LED led_8 (.in(_7486_1_pin11));
  LED led_9 (.in(_7486_1_pin6));
  LED led_10 (.in(_7486_1_pin8));
  not not_3 (not_3_out, _7421_2_pin6);
  D_FF d_ff_1 (.D(_7486_1_pin11), .C(clk), .Q(d_ff_1_q));  // open: nQ
  _74163 _74163_7 (
    .pin1(not_3_out), .pin2(clk), .pin3(1'b0), .pin4(1'b0), .pin5(1'b0), .pin6(1'b0), .pin7(1'b1),
    .pin8(1'b0), .pin9(1'b1), .pin10(d_ff_1_q), .pin11(a3), .pin12(a2), .pin13(a1), .pin14(a0),
    .pin15(_74163_7_pin15), .pin16(1'b1));
  // Probe on {a18, a17, a16, a15, a14, a13, a12, a11, a10, a9, a8, a7, a6, a5, a4, a3, a2, a1, a0}
  _74163 _74163_8 (
    .pin1(not_3_out), .pin2(clk), .pin3(1'b0), .pin4(1'b0), .pin5(1'b0), .pin6(1'b0), .pin7(1'b1),
    .pin8(1'b0), .pin9(1'b1), .pin10(_74163_7_pin15), .pin11(a7), .pin12(a6), .pin13(a5), .pin14(a4),
    .pin15(_74163_8_pin15), .pin16(1'b1));
  _74163 _74163_9 (
    .pin1(not_3_out), .pin2(clk), .pin3(1'b0), .pin4(1'b0), .pin5(1'b0), .pin6(1'b0), .pin7(1'b1),
    .pin8(1'b0), .pin9(1'b1), .pin10(_74163_8_pin15), .pin11(a11), .pin12(a10), .pin13(a9), .pin14(a8),
    .pin15(_74163_9_pin15), .pin16(1'b1));
  _74163 _74163_10 (
    .pin1(not_3_out), .pin2(clk), .pin3(1'b0), .pin4(1'b0), .pin5(1'b0), .pin6(1'b0), .pin7(1'b1),
    .pin8(1'b0), .pin9(1'b1), .pin10(_74163_9_pin15), .pin11(a15), .pin12(a14), .pin13(a13), .pin14(a12),
    .pin15(_74163_10_pin15), .pin16(1'b1));
  _74163 _74163_11 (
    .pin1(not_3_out), .pin2(clk), .pin3(1'b0), .pin4(1'b0), .pin5(1'b0), .pin6(1'b0), .pin7(1'b1),
    .pin8(1'b0), .pin9(1'b1), .pin10(_74163_10_pin15), .pin12(a18), .pin13(a17), .pin14(a16), .pin16(1'b1));  // open: pin11, pin15

  // Notes on the sheet:
  //   74LS279
  //   480 lines
  //   490 lines
  //   492 lines
  //   525 lines
  //   640 pixels reached
  //   656 pixels reached
  //   752 pixels reached
  //   800 pixels reached
  //   HSYNC
  //   SEND_DATA
  //   VSYNC
endmodule
